# Fritzing sketch Se_02_ee_Esquemática (saved by Fritzing 0.9.3b)
breadboards: 1

parts:
  Arduino_UNO = Arduino Uno (Rev3) - ICSP
  R1 = Photocell (LDR) [package=THT]
  YL-83_-_Control_Board1 = YL-83 Rain Sensor - Control Board
  YL-83_-_Detection_Board1 = YL-83 Rain Sensor - Detection Board
  Display_OLED_128x64_i2c = Grove OLED 128x96
  R3 = Resistor [tolerance=±5% resistance=10 package="0603 [SMD]"]
  DHT22 = DHT22 Humidity and Temperature Sensor
  R4 = Resistor [tolerance=±5% resistance=10 package="0603 [SMD]"]

nets:
  N1: Arduino_UNO.A0, R1.pin_1, R4.Pin_0
  N2: Arduino_UNO.A2, YL-83_-_Control_Board1.AO
  N3: Arduino_UNO.A5/SCL, Display_OLED_128x64_i2c.SCL
  VCC: Arduino_UNO.5V, R1.pin_0, YL-83_-_Control_Board1.VCC, Display_OLED_128x64_i2c.VCC, R3.Pin_0, DHT22.VDD
  N4: Arduino_UNO.ICSP_MOSI, Display_OLED_128x64_i2c.SDA
  GND: Arduino_UNO.GND, YL-83_-_Control_Board1.GND, Display_OLED_128x64_i2c.GND, DHT22.GND, R4.Pin_1
  N5: Arduino_UNO.D2, R3.Pin_1, DHT22.DATA
  N6: Arduino_UNO.D7, YL-83_-_Control_Board1.DO
  N7: YL-83_-_Control_Board1.POS, YL-83_-_Detection_Board1.POS
  N8: YL-83_-_Control_Board1.NEG, YL-83_-_Detection_Board1.NEG

custom parts:
  YL-83 Rain Sensor - Control Board: The YL-83 is a rain sensor that has more resistance when dry and less resistance when wet. The module runs at 5V.
  YL-83 Rain Sensor - Detection Board: The YL-83 is a rain sensor that has more resistance when dry and less resistance when wet. The module runs at 5V.
