# Fritzing sketch Se_02_grafica (saved by Fritzing 0.9.3b)
breadboards: 1

parts:
  Componente3 = Arduino Uno (Rev3) - ICSP
  R1 = Photocell (LDR) [package=THT]
  YL-83_-_Control_Board1 = YL-83 Rain Sensor - Control Board
  YL-83_-_Detection_Board1 = YL-83 Rain Sensor - Detection Board
  Grove1 = Grove OLED 128x96
  R3 = Resistor [tolerance=±5% resistance=10 package="0603 [SMD]"]
  R4 = Resistor [tolerance=±5% resistance=10 package="0603 [SMD]"]
  DHT1 = DHT22 Humidity and Temperature Sensor

nets:
  N1: Componente3.A0, R1.pin_1, R3.Pin_0
  N2: Componente3.A2, YL-83_-_Control_Board1.DO
  N3: Componente3.A4/SDA, Grove1.SDA
  N4: Componente3.A5/SCL, Grove1.SCL
  N5: Componente3.D2, R4.Pin_1, DHT1.DATA
  N6: Componente3.D7, YL-83_-_Control_Board1.AO
  VCC: Componente3.5V, R1.pin_0, YL-83_-_Control_Board1.VCC, Grove1.VCC, R4.Pin_0, DHT1.VDD
  GND: Componente3.GND, YL-83_-_Control_Board1.GND, Grove1.GND, R3.Pin_1, DHT1.GND
  N7: YL-83_-_Control_Board1.POS, YL-83_-_Detection_Board1.POS
  N8: YL-83_-_Control_Board1.NEG, YL-83_-_Detection_Board1.NEG

custom parts:
  YL-83 Rain Sensor - Control Board: The YL-83 is a rain sensor that has more resistance when dry and less resistance when wet. The module runs at 5V.
  YL-83 Rain Sensor - Detection Board: The YL-83 is a rain sensor that has more resistance when dry and less resistance when wet. The module runs at 5V.
